# Fritzing sketch schema (saved by Fritzing 0.9.3b)
breadboards: 1

parts:
  RHT1 = Humidity and Temperature Sensor RHT03
  Part2 = Arduino Uno (Rev3)
  Q1 = Basic FET N-Channel [package="DPak [SMD]"]
  DS2 = DS18B20 1-Wire Temperature Sensor Probe Cable
  LED2 = RGB LED (com. cathode, rgb) [package="5 mm [THT]"]
  JACK1 = 2.1mm Barrel Jack with Terminal Block
  F1 = Fan - Ventilador [package=THT]
  LCD1 = LCD screen
  R2 = Resistor [tolerance=±5% resistance=1.2k package=THT]
  R1 = Resistor [tolerance=±5% resistance=10k package=THT]
  R3 = Resistor [tolerance=±5% resistance=4.7 package=THT]

nets:
  VDD: RHT1.Vcc, Part2.5V, DS2.VDD, LCD1.VDD, LCD1.LED+, R1.Pin_0, R3.Pin_1
  N1: RHT1.Data-signal, Part2.D7
  GND: RHT1.GND_1, Part2.GND, Q1.source, DS2.GND, LED2.blue_anode, JACK1.NEG, LCD1.VSS, LCD1.R/W, LCD1.LED-, R2.Pin_0
  N2: Part2.D8, LCD1.E
  N3: Part2.D9_PWM, LED2.green_anode
  N4: Part2.D10_PWM/SS, LED2.common_cathode
  N5: Part2.D11_PWM/MOSI, LED2.red_anode
  N6: Part2.D12/MISO, LCD1.RS
  N7: Part2.D13/SCK, DS2.DQ, R3.Pin_0
  N8: Part2.D2, LCD1.DB7
  N9: Part2.D3_PWM, LCD1.DB6
  N10: Part2.D4, LCD1.DB5
  N11: Part2.D5_PWM, LCD1.DB4
  N12: Part2.D6_PWM, Q1.Gate
  N13: Q1.drain, F1.GND
  N14: JACK1.POS, F1.5V
  N15: LCD1.V0, R2.Pin_1, R1.Pin_1

custom parts:
  Fan - Ventilador: Ventilador de 2 pines, se encuentra comunmente en computadoras de escritorio
